# Fritzing sketch Quadcopter Wiring (saved by Fritzing 0.9.3b)

parts:
  Raspberry_Pi_1 = Raspberry Pi 3 [part_number=RPI-3-V1.2]
  GY1 = GY-5150 (MPU-9150) [form="♀ (female)" package=THT]  # not connected
  Part1 = ESC MLF1218
  920KV_Motor1 = DJI 920 KV Motor
  Part2 = ESC MLF1218
  Part3 = ESC MLF1218
  Part4 = ESC MLF1218
  920KV_Motor2 = DJI 920 KV Motor
  920KV_Motor3 = DJI 920 KV Motor
  920KV_Motor4 = DJI 920 KV Motor
  U1 = mystery part, 3 pins [chip_label=?]
  U2 = mystery part, 3 pins [chip_label=?]
  U3 = mystery part, 3 pins [chip_label=?]
  U4 = mystery part, 3 pins [chip_label=?]
  Power_and_Ground = female pin header, 2 pins [form="♀ (female)"]  # not connected

nets:
  N1: Raspberry_Pi_1.GPIO6, U1.pin1
  N2: Raspberry_Pi_1.GPIO13, U2.pin1
  N3: Raspberry_Pi_1.GPIO19, U3.pin1
  N4: Raspberry_Pi_1.GPIO26, U4.pin1
  N5: Part1.GND*, 920KV_Motor2.w
  N6: Part1.PPM, 920KV_Motor1.v, Part4.+5, 920KV_Motor2.v
  N7: Part1.+5, 920KV_Motor2.u
  N8: 920KV_Motor1.w, Part4.GND*
  N9: 920KV_Motor1.u, Part4.PPM
  N10: Part2.GND*, 920KV_Motor3.w
  N11: Part2.PPM, 920KV_Motor3.v
  N12: Part2.+5, 920KV_Motor3.u
  N13: Part3.GND*, 920KV_Motor4.w
  N14: Part3.PPM, 920KV_Motor4.u
  N15: Part3.+5, 920KV_Motor4.v

custom parts:
  GY-5150 (MPU-9150): Placa GY-5150 basada en conjunto de acelerómetro+giroscopios+magnetómetro MPU-9150
  ESC MLF1218: ESC (Electronic Speed Control) for Cheerson CX-20 quadcopter
  DJI 920 KV Motor: DJI Brushless Outrunner 2212/920K Motor F330-550
